// Logisim project mini6.circ as structural Verilog: 1 circuit, main circuit main
module main (
  input  in_1,
  input  in_2,
  input  in_3,
  input  in_4,
  input  in_5,
  input  R_input,
  input  in_7,
  input  in_8,
  input  in_9,
  input  in_10,
  input  in_11,
  input  in_12,
  input  in_13,
  input  in_14,
  input  in_15,
  input  in_16,
  input  in_17,
  input  in_18,
  input  in_19,
  output out_20,
  output out_21,
  output out_22,
  output out_23,
  output out_24,
  output out_25,
  output out_26,
  output out_27,
  output out_28,
  output out_29,
  output out_30,
  output out_31,
  output out_32
);

  wire and_1_out, and_2_out, and_4_out, and_5_out, and_6_out, and_7_out, and_8_out, and_9_out, and_10_out,
       and_11_out, and_12_out, and_13_out, and_14_out, and_15_out, and_16_out, and_17_out, and_18_out,
       and_20_out, c0, c1, c2, clk, l0, L1, l1_t, L2, l2_t, L3, l3_t, or_2_out, or_5_out, or_8_out, r0, R1,
       r1_t, R2, r2_t, R3, r3_t, xor_3_out, xor_4_out, xor_5_out, xor_6_out;

  D_Flip_Flop d_ff_1 (.D(in_14), .clk(clk), .Q(L3));  // open: Qn, preset, reset
  and and_1 (and_1_out, L1, R1);
  xor xor_1 (out_31, L1, R1);
  xor xor_2 (out_30, and_1_out, xor_3_out);
  D_Flip_Flop d_ff_2 (.D(in_15), .clk(clk), .Q(L2));  // open: Qn, preset, reset
  xor xor_3 (xor_3_out, L2, R2);
  xor xor_4 (xor_4_out, out_30, and_2_out);
  D_Flip_Flop d_ff_3 (.D(in_11), .clk(clk), .Q(R3));  // open: Qn, preset, reset
  D_Flip_Flop d_ff_4 (.D(in_16), .clk(clk), .Q(L1));  // open: Qn, preset, reset
  and and_2 (and_2_out, L2, R2);
  xor xor_5 (xor_5_out, L3, R3);
  nor nor_1 (out_29, xor_4_out, xor_5_out);
  and and_3 (out_28, ~out_29, xor_5_out);  // AND_Gate
  D_Flip_Flop d_ff_5 (.D(in_12), .clk(clk), .Q(R2));  // open: Qn, preset, reset
  and and_4 (and_4_out, L3, R3);
  D_Flip_Flop d_ff_6 (.D(in_13), .clk(clk), .Q(R1));  // open: Qn, preset, reset
  and and_5 (and_5_out, r3_t, c2);
  and and_6 (and_6_out, l3_t, c2);
  and and_7 (and_7_out, r3_t, l3_t);
  or or_1 (out_24, and_5_out, and_6_out, and_7_out);
  or or_2 (or_2_out, r3_t, l3_t, c2);
  and and_8 (and_8_out, ~out_24, or_2_out);  // AND_Gate
  and and_9 (and_9_out, r2_t, c1);
  and and_10 (and_10_out, r3_t, l3_t, c2);
  or or_3 (out_20, and_8_out, and_10_out);
  and and_11 (and_11_out, l2_t, c1);
  and and_12 (and_12_out, r2_t, l2_t);
  or or_4 (c2, and_9_out, and_11_out, and_12_out);
  or or_5 (or_5_out, r2_t, l2_t, c1);
  and and_13 (and_13_out, ~c2, or_5_out);  // AND_Gate
  and and_14 (and_14_out, r1_t, c0);
  and and_15 (and_15_out, r2_t, l2_t, c1);
  or or_6 (out_21, and_13_out, and_15_out);
  and and_16 (and_16_out, l1_t, c0);
  and and_17 (and_17_out, r1_t, l1_t);
  or or_7 (c1, and_14_out, and_16_out, and_17_out);
  or or_8 (or_8_out, r1_t, l1_t, c0);
  and and_18 (and_18_out, ~c1, or_8_out);  // AND_Gate
  and and_19 (c0, r0, l0);
  and and_20 (and_20_out, r1_t, l1_t, c0);
  or or_9 (out_22, and_18_out, and_20_out);
  xor xor_6 (xor_6_out, r0, l0);
  and and_21 (out_23, ~c0, xor_6_out);  // AND_Gate
  Clock clock_1 (.out(clk));
  D_Flip_Flop d_ff_7 (.D(in_1), .clk(clk), .Q(r3_t));  // open: Qn, preset, reset
  D_Flip_Flop d_ff_8 (.D(in_7), .clk(clk), .Q(l3_t));  // open: Qn, preset, reset
  D_Flip_Flop d_ff_9 (.D(in_2), .clk(clk), .Q(r2_t));  // open: Qn, preset, reset
  D_Flip_Flop d_ff_10 (.D(in_8), .clk(clk), .Q(l2_t));  // open: Qn, preset, reset
  D_Flip_Flop d_ff_11 (.D(in_3), .clk(clk), .Q(r1_t));  // open: Qn, preset, reset
  D_Flip_Flop d_ff_12 (.D(in_9), .clk(clk), .Q(l1_t));  // open: Qn, preset, reset
  D_Flip_Flop d_ff_13 (.D(in_4), .clk(clk), .Q(r0));  // open: Qn, preset, reset
  D_Flip_Flop d_ff_14 (.D(in_10), .clk(clk), .Q(l0));  // open: Qn, preset, reset

  // Other names for the same wires on the sheet: o0 = out_23; O1 = out_31; o1_t = out_22; O2 = out_30; o2_t = out_21;
  //   O3 = out_29; o3_t = out_20; O4 = out_28; ov = out_24

  // Notes on the sheet:
  //   add/sub command
  //   L input
  //   A-out output
  //   status output
endmodule
